// Logisim project allLogicGates.circ as structural Verilog: 1 circuit, main circuit main
module main (
  input  in_1,
  input  in_2,
  input  in_3,
  input  in_4,
  input  in_5,
  input  in_6,
  input  in_7,
  input  in_8,
  input  in_9,
  input  in_10,
  input  in_11,
  input  in_12,
  input  in_13,
  input  in_14,
  output out_15,
  output out_16,
  output out_17,
  output out_18,
  output out_19,
  output out_20,
  output Buffer,
  output out_22
);

  and and_1 (out_15, in_1, in_4);
  or or_1 (out_20, in_9, in_12);
  not not_1 (out_22, in_14);
  nand nand_1 (out_16, in_2, in_5);
  nor nor_1 (out_18, in_7, in_10);
  xnor xnor_1 (out_17, in_3, in_6);
  xor xor_1 (out_19, in_8, in_11);
  buf buffer_1 (Buffer, in_13);

  // Notes on the sheet:
  //   And
  //   Or
  //   Not
  //   Nor
  //   Nand
  //   X Nor
  //   X Or
endmodule
