// Logisim project decoder.circ as structural Verilog: 1 circuit, main circuit main
module main (
  input  _2,
  input  _1,
  input  _3_8_Decoder,
  output _0,
  output _1_2,
  output _2_2,
  output _3,
  output _4,
  output _5,
  output _6,
  output _7
);

  wire not_1_out, not_2_out, not_3_out;

  not not_1 (not_1_out, _2);
  not not_2 (not_2_out, _1);
  not not_3 (not_3_out, _3_8_Decoder);
  and and_1 (_0, not_3_out, not_2_out, not_1_out);
  and and_2 (_1_2, _3_8_Decoder, not_2_out, not_1_out);
  and and_3 (_2_2, not_3_out, _1, not_1_out);
  and and_4 (_3, _1, _3_8_Decoder, not_1_out);
  and and_5 (_4, not_3_out, not_2_out, _2);
  and and_6 (_5, _3_8_Decoder, not_2_out, _2);
  and and_7 (_6, not_3_out, _1, _2);
  and and_8 (_7, _2, _1, _3_8_Decoder);
endmodule
