// Logisim project eightBitRegister.circ as structural Verilog: 1 circuit, main circuit main
module main (
  input  [2:0] Read_Register_1,
  input  [2:0] Read_Register_2,
  input  [2:0] Read_Register_3,
  input  [7:0] Data_you_want_to_Write,
  input  Clock,
  input  Register_Write,
  output [7:0] out_7,
  output [7:0] out_8
);

  wire and_1_out, and_2_out, and_3_out, and_4_out, and_5_out, and_6_out, and_7_out, and_8_out,
       decoder_1_out0, decoder_1_out1, decoder_1_out2, decoder_1_out3, decoder_1_out4, decoder_1_out5,
       decoder_1_out6, decoder_1_out7;
  wire [7:0] register_1_q, register_2_q, register_3_q, register_4_q, register_5_q, register_6_q,
       register_7_q, register_8_q;

  Decoder #(.select(3)) decoder_1 (
    .out0(decoder_1_out0), .out1(decoder_1_out1), .out2(decoder_1_out2), .out3(decoder_1_out3),
    .out4(decoder_1_out4), .out5(decoder_1_out5), .out6(decoder_1_out6), .out7(decoder_1_out7),
    .sel(Read_Register_1));  // open: en
  and and_1 (and_1_out, decoder_1_out0, Register_Write);
  and and_2 (and_2_out, decoder_1_out1, Register_Write);
  and and_3 (and_3_out, decoder_1_out2, Register_Write);
  and and_4 (and_4_out, decoder_1_out3, Register_Write);
  and and_5 (and_5_out, decoder_1_out4, Register_Write);
  and and_6 (and_6_out, decoder_1_out5, Register_Write);
  and and_7 (and_7_out, decoder_1_out6, Register_Write);
  and and_8 (and_8_out, decoder_1_out7, Register_Write);
  Register register_1 (.D(Data_you_want_to_Write), .Q(register_1_q), .clk(Clock), .clr(and_1_out));  // open: en
  Register register_2 (.D(Data_you_want_to_Write), .Q(register_2_q), .clk(Clock), .clr(and_2_out));  // open: en
  Register register_3 (.D(Data_you_want_to_Write), .Q(register_3_q), .clk(Clock), .clr(and_3_out));  // open: en
  Register register_4 (.D(Data_you_want_to_Write), .Q(register_4_q), .clk(Clock), .clr(and_4_out));  // open: en
  Register register_5 (.D(Data_you_want_to_Write), .Q(register_5_q), .clk(Clock), .clr(and_5_out));  // open: en
  Register register_6 (.D(Data_you_want_to_Write), .Q(register_6_q), .clk(Clock), .clr(and_6_out));  // open: en
  Register register_7 (.D(Data_you_want_to_Write), .Q(register_7_q), .clk(Clock), .clr(and_7_out));  // open: en
  Register register_8 (.D(Data_you_want_to_Write), .Q(register_8_q), .clk(Clock), .clr(and_8_out));  // open: en
  Multiplexer #(.select(3), .width(8)) multiplexer_1 (
    .in0(register_1_q), .in1(register_2_q), .in2(register_3_q), .in3(register_4_q), .in4(register_5_q),
    .in5(register_6_q), .in6(register_7_q), .in7(register_8_q), .out(out_7), .sel(Read_Register_3));  // open: en
  Multiplexer #(.select(3), .width(8)) multiplexer_2 (
    .in0(register_1_q), .in1(register_2_q), .in2(register_3_q), .in3(register_4_q), .in4(register_5_q),
    .in5(register_6_q), .in6(register_7_q), .in7(register_8_q), .out(out_8), .sel(Read_Register_2));  // open: en
endmodule
